# Fritzing sketch arduino-attiny (saved by Fritzing 0.9.3b)
breadboards: 1

parts:
  Part1 = Arduino Uno (Rev3)
  U1 = ATTINY45 [package=dip]
  10uF_capacitor = Capacitor Polarized [package=panasonic_c]

nets:
  N1: Part1.D10_PWM/SS, U1.PB5(NRES)
  N2: Part1.D11_PWM/MOSI, U1.PB0(MOSI)
  N3: Part1.D12/MISO, U1.PB1(MISO)
  N4: Part1.D13/SCK, U1.PB2(SCK_ADC1)
  N5: Part1.RESET, 10uF_capacitor.+
  5V: Part1.5V, U1.VCC
  GND: Part1.GND, U1.GND, 10uF_capacitor.-

notes:
  Arduino Uno - Attiny85
  5V ------> Vcc
  Gnd ----> Gnd
  Pin 13 -> Pin 2
  Pin 12 -> Pin 1
  Pin 10 -> Reset
